# Fritzing sketch Perfboard (saved by Fritzing 0.9.1b)
circuit board: 5cm x 10cm

parts:
  ATTiny85 = attiny85 [package=dip]
  SN754410 = H-Bridge [package=THT]
  IC1 = Voltage Regulator [package=to220-igo]
  C2 = Capacitor Polarized [package=panasonic_c]
  C3 = Capacitor [package=cap-pth-small2]
  C5 = Capacitor Polarized [package=panasonic_c]  # not connected
  C6 = Capacitor [package=cap-pth-small2]  # not connected
  C7 = Capacitor [package=cap-pth-small2]  # not connected
  R1 = Resistor [package="2010 [SMD]"]  # not connected
  LED1 = LED - 5mm [color="Red (633nm)" package="5 mm [THT]"]  # not connected
  R2 = Resistor [tolerance=±5% resistance=220 package=THT]

nets:
  N1: ATTiny85.Pin_1, R2.Pin_1
  N2: ATTiny85.Pin_5, SN754410.2A
  N3: ATTiny85.Pin_6, SN754410.1A
  GND1: SN754410.GND1, SN754410.GND4
  GND2: SN754410.GND2, SN754410.GND3
  N4: IC1.GND, C2.-, C3.2
  N5: IC1.OUT, C2.+, C3.1, R2.Pin_0

notes:
  V+
  V-
